# Fritzing sketch Coordinator_Mechanical Arm (saved by Fritzing 0.9.3b)
breadboards: 1

parts:
  Bauteil1 = Arduino Uno (Rev3)
  R1 = Rotary Potentiometer (Small) [maximum_resistance=100kΩ package=THT]
  R2 = Rotary Potentiometer (Small) [maximum_resistance=100kΩ package=THT]
  R3 = Rotary Potentiometer (Small) [maximum_resistance=100kΩ package=THT]
  M1 = Stepper Motor - Bipolar
  J1 = Basic Servo
  J2 = Basic Servo
  VCC1 = Battery block 9V
  IC1 = H-Bridge [package=THT]

nets:
  N1: Bauteil1.A0, R2.wiper
  N2: Bauteil1.A1, R1.wiper
  N3: Bauteil1.A2, R3.wiper
  N4: Bauteil1.D10_PWM/SS, J2.pulse
  N5: Bauteil1.D11_PWM/MOSI, J1.pulse
  N6: Bauteil1.GND, R1.leg1, R1.leg2, R2.leg1, R2.leg2, R3.leg1, R3.leg2
  N7: Bauteil1.D2, IC1.VCC2
  N8: Bauteil1.D3_PWM, IC1.2A
  N9: Bauteil1.D4, IC1.2Y
  N10: Bauteil1.D6_PWM, IC1.GND2
  N11: M1.A, IC1.VCC1
  N12: M1.C, IC1.4A
  N13: M1.B, IC1.4Y
  N14: M1.D, IC1.GND4
  N15: VCC1.-, IC1.3A
  N16: VCC1.+, IC1.3_4EN

notes:
  this H-Bridge is not the one we used, but Fritzing didnt have that one and I am lazy.
  It's not even connected in the Right way.
  We used a 12V Power supply.
  This is for manually Controlling the mechanical Arm via Potentiometers. If you have to adjust some coordinates on the board you can just plug this in.
